# Fritzing sketch esp_bno (saved by Fritzing 0.9.4)
stripboards: 1

parts:
  U1 = ESP32S-HiLetgo [part_number=ESP32S-HiLetgo]
  Bauteil1 = Adafruit BME280
  J2 = male pin header, 3 pins [form="♂ (male)"]
  J3 = male pin header, 3 pins [form="♂ (male)"]
  J4 = male pin header, 3 pins [form="♂ (male)"]
  IC1 = IC, SIP package, 11 pins [chip_label=BNO_Slave]
  IC2 = IC, SIP package, 7 pins [chip_label=BNO_Master]
  J5 = male pin header, 3 pins [form="♂ (male)"]
  R2 = Vertical Resistor [tolerance=±5% resistance=1k package=THT]
  J6 = male pin header, 4 pins [form="♂ (male)"]
  J7 = male pin header, 4 pins [form="♂ (male)"]
  R3 = Resistor [tolerance=±5% resistance=2.2k package="0805 [SMD]"]
  U2 = mystery part, 6 pins [chip_label=GPS]
  U4 = Mystery Part - 4 pins [chip_label=? package=THT]  # not connected

nets:
  VIN: U1.3.3, Bauteil1.VIN, Bauteil1.3.3V, IC2.pin7
  GND: U1.GND, Bauteil1.GND, J2.pin1, J3.pin1, J4.pin1, IC1.pin10, IC2.pin6, J5.pin1, J6.pin1, J7.pin1, R3.Pin_0, U2.pin2
  N1: U1.GPIO9, U1.GPIO11
  N2: U1.VIN, J2.pin2, J3.pin2, J4.pin2, J5.pin2, J6.pin2, J7.pin2
  N3: U1.GPIO6, U1.GPIO8
  N4: U1.GPIO15, J2.pin3
  N5: U1.GPIO2, J3.pin3
  N6: U1.GPIO0, J4.pin3
  N7: U1.GPIO4, J5.pin3
  N8: U1.GPIO16, R2.Pin_0, R3.Pin_1
  N9: U1.GPIO17, IC1.pin8, R2.Pin_1, J6.pin3, J6.pin4, U2.pin1
  N10: U1.GPIO5, IC1.pin9, U2.pin6
  N11: U1.GPIO18, J7.pin3, J7.pin4
  N12: U1.GPIO3, U1.GPIO1
  N13: U1.GPIO22, IC1.pin4
  N14: U1.GPIO23, IC1.pin5
  N15: Bauteil1.SCK/SCL, IC2.pin5
  N16: Bauteil1.SDO/ADR, Bauteil1.SDI/SDA, IC2.pin3, IC2.pin4
  N17: Bauteil1.CS, IC2.pin2
  N18: IC1.pin11, U2.pin5

notes:
  +5V
  GND
  SCL
  SDA
  X
  trig
  echo

custom parts:
  ESP32S-HiLetgo: HiLetgo ESP-WROOM-32 ESP32 ESP-32S Development Board 2.4GHz Dual-Mode WiFi + Bluetooth Dual Cores Microcontroller The ESP32 integrated with Antenna switches, RF Balun, power amplifiers, low-noise amplifiers, filters, and management modules, and the entire solution occupies the least area of PCB. 2.4 GHz Wi-Fi plus Bluetooth dual-mode chip, with TSMC Ultra-low power consumption 40nm technology,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
  Adafruit BME280: Bosch has stepped up their game with their new BME280 sensor, an environmental sensor with temperature, barometric pressure and humidity! This sensor is great for all sorts of weather/environmental sensing and can even be used in both I2C and SPI! This precision sensor from Bosch is the best low-cost sensing solution for measuring humidity with ±3% accuracy, barometric pressure with ±1 hPa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
  Vertical Resistor: A generic resistor (0.25W)
  Mystery Part - 4 pins: A dummy, proxy, ersatz, stand-in part for whatever you want. With 4 pins on a 300mil inline pin header footprint.
